# Fritzing sketch momobox (saved by Fritzing 0.9.10b)
stripboards: 1
perfboards: 2

parts:
  Mod1 = Raspberry Pi Pico
  Part1 = Adafruit PAM8302 [part_number="Adafruit #2130"]
  Part2 = Adafruit SDIO microSD Breakout
  BAT1 = Battery Holders [package=battery-aa]
  SP1 = SPEAKER [package=pcb_mount_speaker]
  R1 = Resistor [tolerance=±5% power=0.25 resistance=4.7k package=THT]
  C1 = Ceramic Capacitor [capacitance=100nF voltage=35V package="100 mil [THT, multilayer]"]
  Part5 = RFID-RC522-v2
  3-pins_Hall_Effect_Sensor1 = mystery part, 3 pins [chip_label="Hall Effect Sensor"]
  R2 = Resistor [tolerance=±5% power=0.25 resistance=10k package=THT]

nets:
  N1: Mod1.pin_1, Part5.RST
  N2: Mod1.pin_2, Part5.SDA
  N3: Mod1.pin_4, Part5.SCK
  N4: Mod1.pin_5, Part5.MOSI
  N5: Mod1.pin_6, Part5.MISO
  GND: Mod1.pin_8, Mod1.pin_13, Mod1.pin_23, Mod1.pin_38, Part1.GND, Part1.AIN-, Part2.GND, BAT1.-, C1.0, Part5.GND, 3-pins_Hall_Effect_Sensor1.pin2
  hall: Mod1.pin_11, 3-pins_Hall_Effect_Sensor1.pin3, R2.Pin_1
  N6: Mod1.pin_15, Part2.DI
  N7: Mod1.pin_16, Part2.DO
  N8: Mod1.pin_17, Part2.CS
  N9: Mod1.pin_19, Part2.SCLK
  N10: Mod1.pin_21, R1.Pin_0
  N11: Mod1.pin_29, Part2.CARDDET
  3V3: Mod1.pin_36, Part1.VCC, Part2.3.3V, Part5.3.3V, 3-pins_Hall_Effect_Sensor1.pin1, R2.Pin_0
  N12: Mod1.pin_39, BAT1.+
  N13: Part1.AIN+, R1.Pin_1, C1.1
  N14: Part1.VO+, SP1.+
  N15: Part1.VO-, SP1.-

custom parts:
  Raspberry Pi Pico: Raspberry Pi Pico. Based around the RP2040 microcontroller the Pico is a low cost microcontroller device bringing Raspberry Pi quality, cost, and easy of use to the microcontroller space. Jan 2021, Split part in to two versions: tht (this one) and SMD. This one will drill holes for a .1 in header in pcb to allow plugging in the module as well as providing pads to solder the module to the top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
  Adafruit PAM8302: This super small mono amplifier is surprisingly powerful - able to deliver up to 2.5 Watts into 4-8 ohm impedance speakers. Inside the miniature chip is a class D controller, able to run from 2.0V-5.5VDC. Since the amp is a class D, its very efficient (over 90% efficient when driving an 8Ω speaker at over half a Watt) - making it perfect for portable and battery-powered projects. It has built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
  RFID-RC522-v2: A simple China made RFID-RC522 Reader; do check the pin labels, as this is a MFRC522 based clone.
